# Fritzing sketch Fritzing Sketch (saved by Fritzing 0.8.7b)
breadboards: 1

parts:
  Eleman1 = SRF05 Ultrasonic Rangefinder
  Eleman2 = Arduino Uno (Rev3)
  U1 = LCD-16X2 [package=lcd-16x2]
  R1 = Rotary Potentiometer (Small) [maximum_resistance=100kΩ package=THT]  # not connected
  R2 = Resistor [tolerance=±5% resistance=220 package=THT]
  J2 = Piezo Speaker

nets:
  VCC: Eleman1.VCC, Eleman2.5V, U1.VDD, R2.Pin_0
  N1: Eleman1.Trig, Eleman2.D10_PWM/SS
  N2: Eleman1.Echo, Eleman2.D9_PWM
  GND: Eleman1.GND, Eleman2.GND, U1.VSS, U1.R_W, U1.K, J2.pin1
  N3: Eleman2.D11_PWM/MOSI, U1.RS
  N4: Eleman2.D12/MISO, U1.E
  N5: Eleman2.D2, U1.DB7
  N6: Eleman2.D3_PWM, U1.DB6
  N7: Eleman2.D4, U1.DB5
  N8: Eleman2.D5_PWM, U1.DB4
  N9: Eleman2.D6_PWM, J2.pin2
  N10: U1.A, R2.Pin_1
